# Fritzing sketch Zumo (saved by Fritzing 0.9.3b)
breadboards: 2

parts:
  Part1 = Arduino Uno (Rev3)
  Part2 = Bluetooth HC-05 Macho
  hc-sr1 = hc-sr04

nets:
  N1: Part1.A4/SDA, hc-sr1.Trig, hc-sr1.Echo
  N2: Part1.D4, Part2.TXD
  N3: Part1.D5_PWM, Part2.RXD
  3V3: Part1.3V3, Part2.VCC
  5V: Part1.5V, hc-sr1.VCC
  GND: Part1.GND, Part2.GND, hc-sr1.GND
